// Logisim project cpu.circ as structural Verilog: 8 circuits, main circuit Imm_Gen
module main (
  input  [31:0] INSTRUCTION,
  input  CLOCK,
  output [31:0] FETCH_ADDRESS,
  output [31:0] s0_Value,
  output [31:0] s1_Value,
  output [31:0] t0_Value,
  output [31:0] t1_Value,
  output [31:0] a0_Value,
  output [31:0] ra_Value,
  output [31:0] sp_Value
);

  wire ASel, BrEq, BrLt, BrUn, BSel, MEM_p1, MEM_p2, MEM_p5, MemRW, PCSel, RegWEn;
  wire [1:0] LoadSel, WBSel;
  wire [2:0] ImmSel;
  wire [3:0] ALUSel;
  wire [7:0] multiplexer_6_out;
  wire [15:0] multiplexer_7_out;
  wire [31:0] adder_2_out, ALURes, bit_extender_1_out, bit_extender_2_out, Imm, LoadData, main_1_read_data_1,
       MemOutput, multiplexer_1_out, multiplexer_2_out, multiplexer_3_out, multiplexer_4_out,
       multiplexer_5_out, multiplexer_8_out, PC_4, PC_Ex, register_2_q, register_3_q, shifter_1_out,
       shifter_2_out, shifter_3_out, shifter_4_out, Write;

  Multiplexer #(.width(32), .enable("false")) multiplexer_1 (
    .in0(PC_4), .in1(shifter_1_out), .out(multiplexer_1_out), .sel(PCSel));
  Shifter #(.width(32), .shift("lr")) shifter_1 (.in(ALURes), .\dist (5'b00010), .out(shifter_1_out));
  Register #(.width(32)) PC (.D(multiplexer_1_out), .Q(FETCH_ADDRESS), .clk(CLOCK));  // open: en, clr
  Adder #(.width(32)) adder_1 (.a(32'h1), .b(FETCH_ADDRESS), .out(PC_4));  // open: cin, cout
  Register #(.width(32)) register_1 (.D(FETCH_ADDRESS), .Q(PC_Ex), .clk(CLOCK));  // open: en, clr
  Multiplexer #(.width(32), .enable("false")) multiplexer_2 (
    .in0(INSTRUCTION), .in1({32{1'b0}}), .out(multiplexer_2_out), .sel(PCSel));
  Multiplexer #(.width(32), .enable("false")) multiplexer_3 (
    .in0(INSTRUCTION), .in1({32{1'b0}}), .out(multiplexer_3_out), .sel(PCSel));
  Register #(.width(32)) register_2 (.D(multiplexer_2_out), .Q(register_2_q), .clk(CLOCK));  // open: en, clr
  Register #(.width(32)) register_3 (.D(multiplexer_3_out), .Q(register_3_q), .clk(CLOCK));  // open: en, clr
  Imm_Gen imm_gen_1 (.in_1(register_2_q), .in_2(ImmSel), .Imm(Imm));
  regfile_main main_1 (
    .Read_Register_1__rs1(register_2_q[19:15]), .Read_Register_2__rs2(register_2_q[24:20]),
    .Write_Register__rd(register_2_q[11:7]), .Write_Data(multiplexer_8_out), .Write_Enable(RegWEn),
    .Read_Data_1(main_1_read_data_1), .Read_Data_2(Write), .s1_Value(s1_Value), .t0_Value(t0_Value),
    .t1_Value(t1_Value), .a0_Value(a0_Value), .s0_Value(s0_Value), .ra_Value(ra_Value), .sp_Value(sp_Value),
    .Clock(CLOCK));
  Control Control (
    .BrEq(BrEq), .instruction(register_3_q), .BrLT(BrLt), .ASel(ASel), .MemRW(MemRW), .BrUn(BrUn),
    .PCSel(PCSel), .ALUSel(ALUSel), .WBSel(WBSel), .RegWEn(RegWEn), .BSel(BSel), .ImmSel(ImmSel),
    .LoadSel(LoadSel));
  Branch_Comp branch_comp_1 (.in_1(main_1_read_data_1), .in_3(Write), .BrUn(BrUn), .BrEq(BrEq), .BrUnLT_LT(BrLt));
  Multiplexer #(.width(32), .enable("false")) multiplexer_4 (
    .in0(main_1_read_data_1), .in1(shifter_2_out), .out(multiplexer_4_out), .sel(ASel));
  Shifter #(.width(32)) shifter_2 (.in(PC_Ex), .\dist (5'b00010), .out(shifter_2_out));
  Multiplexer #(.width(32), .enable("false")) multiplexer_5 (
    .in0(Write), .in1(Imm), .out(multiplexer_5_out), .sel(BSel));
  alu_main main_2 (.Switch(ALUSel), .X(multiplexer_4_out), .Result(ALURes), .Y(multiplexer_5_out));  // open: Equal
  Shifter #(.width(32), .shift("lr")) shifter_3 (.in(ALURes), .\dist (5'b00010), .out(shifter_3_out));
  Multiplexer #(.select(2), .width(8), .enable("false")) multiplexer_6 (
    .in0(MemOutput[7:0]), .in1(MemOutput[15:8]), .in2(MemOutput[23:16]), .in3(MemOutput[31:24]),
    .out(multiplexer_6_out), .sel(ALURes[1:0]));
  Multiplexer #(.width(16), .enable("false")) multiplexer_7 (
    .in0(MemOutput[15:0]), .in1(MemOutput[31:16]), .out(multiplexer_7_out), .sel(ALURes[1]));
  // mem_main MEM: pin names not known; wires that end beside it: MEM_p1, MEM_p2, MemOutput[31:24], MEM_p2, MEM_p5, shifter_3_out, Write, MemRW, CLOCK, MemOutput
  Shifter #(.width(32)) shifter_4 (.in(PC_Ex), .\dist (5'b00010), .out(shifter_4_out));
  assign bit_extender_1_out = {{24{multiplexer_6_out[7]}}, multiplexer_6_out};  // Bit_Extender bit_extender_1
  assign bit_extender_2_out = {{16{multiplexer_7_out[15]}}, multiplexer_7_out};  // Bit_Extender bit_extender_2
  Multiplexer #(.select(2), .width(32), .enable("false")) multiplexer_8 (
    .in0(LoadData), .in1(ALURes), .in2(adder_2_out), .out(multiplexer_8_out), .sel(WBSel));  // open: in3
  Adder #(.width(32)) adder_2 (.a(32'h4), .b(shifter_4_out), .out(adder_2_out));  // open: cin, cout
  Multiplexer #(.select(2), .width(32), .enable("false")) multiplexer_9 (
    .in0(bit_extender_1_out), .in1(bit_extender_2_out), .in2(MemOutput), .out(LoadData), .sel(LoadSel));  // open: in3

  // Other names for the same wires on the sheet: a0[31:0] = a0_Value; byteOff[1:0] = ALURes[1:0]; halfOff = ALURes[1];
  //   clk = CLOCK; fetch_addr[31:0] = FETCH_ADDRESS; PC_If[31:0] = FETCH_ADDRESS; ra[31:0] = ra_Value;
  //   s0[31:0] = s0_Value; s1[31:0] = s1_Value; sp[31:0] = sp_Value; t0[31:0] = t0_Value; t1[31:0] = t1_Value

  // Notes on the sheet:
  //   Output
  //   These are outputs/inputs from run.circ
  //   Inputs
  //   These are DEBUG/TEST outputs from your circuit.
endmodule

module Imm_Gen (
  input  [31:0] in_1,
  input  [2:0] in_2,
  output [31:0] Imm
);

  wire [31:0] B_type, bit_extender_4_out, I_type, J_type, S_type, U_type;

  assign I_type = {{20{in_1[31]}}, in_1[31:20]};  // Bit_Extender bit_extender_1
  assign S_type = {{20{in_1[31]}}, {in_1[31:25], in_1[11:7]}};  // Bit_Extender bit_extender_2
  assign B_type = {{20{in_1[31]}}, {in_1[31:25], in_1[11:8], 1'b0}};  // Bit_Extender bit_extender_3
  assign bit_extender_4_out = {{12{1'b0}}, in_1[31:12]};  // Bit_Extender bit_extender_4
  Shifter #(.width(32)) shifter_1 (.in(bit_extender_4_out), .\dist (5'b01100), .out(U_type));
  assign J_type = {{11{in_1[31]}}, {in_1[31], in_1[19:12], in_1[20], in_1[30:21], 1'b0}};  // Bit_Extender bit_extender_5
  Multiplexer #(.select(3), .width(32), .enable("false")) multiplexer_1 (
    .in0(I_type), .in1(S_type), .in2(B_type), .in3(U_type), .in4(J_type), .out(Imm), .sel(in_2));  // open: in5, in6, in7

  // Other names for the same wires on the sheet: _7 = in_1[7]; _8_11[3:0] = in_1[11:8]; _20_24[4:0] = in_1[24:20];
  //   _25_30[5:0] = in_1[30:25]; _12_14[2:0] = in_1[14:12]; _15_19[4:0] = in_1[19:15]; _31 = in_1[31]
endmodule

module Branch_Comp (
  input  [31:0] in_1,
  input  BrUn,
  input  [31:0] in_3,
  output BrEq,
  output BrUnLT_LT
);

  wire LT, UnLT;

  Comparator #(.width(32)) comparator_1 (.a(in_1), .b(in_3), .eq(BrEq), .lt(LT));  // open: gt
  Comparator #(.width(32), .mode("unsigned")) comparator_2 (.a(in_1), .b(in_3), .lt(UnLT));  // open: gt, eq
  Multiplexer #(.enable("false")) multiplexer_1 (.in0(LT), .in1(UnLT), .out(BrUnLT_LT), .sel(BrUn));

  // Other names for the same wires on the sheet: Input1[31:0] = in_1; Input2[31:0] = in_3
endmodule

module Control (
  input  BrEq,
  input  [31:0] instruction,
  input  BrLT,
  output [1:0] LoadSel,
  output BrUn,
  output PCSel,
  output ASel,
  output MemRW,
  output RegWEn,
  output BSel,
  output [2:0] ImmSel,
  output [1:0] WBSel,
  output [3:0] ALUSel
);

  wire multiplexer_1_out, multiplexer_9_out;
  wire [3:0] multiplexer_2_out, multiplexer_3_out, multiplexer_4_out, multiplexer_5_out, multiplexer_6_out,
       multiplexer_7_out, multiplexer_8_out;

  Multiplexer #(.enable("false")) multiplexer_1 (
    .in0(BrEq), .in1(BrLT), .out(multiplexer_1_out), .sel(instruction[14]));
  OpSelect opselect_1 (
    .Load(1'b1), .I_type_except_load(1'b1), .S_type(1'b0), .R_type(1'b1), .U_type(1'b1), .SB_type(1'b0),
    .jalr(1'b1), .UJ_type(1'b1), .in_9(instruction[6:2]), .To_Control(RegWEn));
  Multiplexer #(.width(4), .enable("false")) multiplexer_2 (
    .in0(4'b0101), .in1(4'b1001), .out(multiplexer_2_out), .sel(instruction[25]));
  Multiplexer #(.width(4), .enable("false")) multiplexer_3 (
    .in0(4'b0000), .in1(4'b1000), .out(multiplexer_3_out), .sel(instruction[25]));
  OpSelect opselect_2 (
    .Load(1'b0), .I_type_except_load(1'b0), .S_type(1'b0), .R_type(1'b0), .U_type(1'b0),
    .SB_type(multiplexer_1_out), .jalr(1'b1), .UJ_type(1'b1), .in_9(instruction[6:2]), .To_Control(PCSel));
  Multiplexer #(.width(4), .enable("false")) multiplexer_4 (
    .in0(4'b0010), .in1(4'b1011), .out(multiplexer_4_out), .sel(instruction[30]));
  Multiplexer #(.width(4), .enable("false")) multiplexer_5 (
    .in0(4'b0100), .in1(4'b1010), .out(multiplexer_5_out), .sel(instruction[25]));
  Multiplexer #(.width(4), .enable("false")) multiplexer_6 (
    .in0(multiplexer_4_out), .in1(4'b0111), .out(multiplexer_6_out), .sel(instruction[25]));
  OpSelect opselect_3 (
    .Load(1'b1), .I_type_except_load(1'b1), .S_type(1'b1), .R_type(1'b0), .U_type(1'b1), .SB_type(1'b1),
    .jalr(1'b1), .UJ_type(1'b1), .in_9(instruction[6:2]), .To_Control(BSel));
  Multiplexer #(.select(3), .width(4), .enable("false")) multiplexer_7 (
    .in0(multiplexer_6_out), .in1(multiplexer_3_out), .in2(4'b0110), .in4(multiplexer_2_out), .in5(4'b0001),
    .in6(multiplexer_5_out), .in7(4'b0011), .out(multiplexer_7_out), .sel(instruction[14:12]));  // open: in3
  OpSelect opselect_4 (
    .Load(1'b0), .I_type_except_load(1'b0), .S_type(1'b0), .R_type(1'b0), .U_type(1'b0), .SB_type(1'b1),
    .jalr(1'b0), .UJ_type(1'b1), .in_9(instruction[6:2]), .To_Control(ASel));
  Multiplexer #(.select(3), .width(4), .enable("false")) multiplexer_8 (
    .in0(4'b0010), .in1(4'b0000), .in2(4'b0110), .in4(4'b0101), .in5(4'b0001), .in6(4'b0100), .in7(4'b0011),
    .out(multiplexer_8_out), .sel(instruction[14:12]));  // open: in3
  OpSelect opselect_5 (
    .Load(1'b0), .I_type_except_load(1'b0), .S_type(1'b1), .R_type(1'b0), .U_type(1'b0), .SB_type(1'b0),
    .jalr(1'b0), .UJ_type(1'b0), .in_9(instruction[6:2]), .To_Control(MemRW));
  WBSelector wbselector_1 (
    .Load(2'b00), .I_type_except_load(2'b01), .R_type(2'b01), .U_type(2'b01), .jalr(2'b10), .UJ_type(2'b10),
    .in_9(instruction[6:2]), .To_Control(WBSel));  // open: S_type, SB_type
  ALUSelector aluselector_1 (
    .Load(4'b0010), .I_type_except_load(multiplexer_8_out), .S_type(4'b0010), .R_type(multiplexer_7_out),
    .U_type(4'b1111), .SB_type(4'b0010), .jalr(4'b0010), .UJ_type(4'b0010), .in_9(instruction[6:2]),
    .To_Control(ALUSel));
  Multiplexer #(.enable("false")) multiplexer_9 (
    .in0(1'b0), .in1(1'b1), .out(multiplexer_9_out), .sel(instruction[13]));
  ImmSelector immselector_1 (
    .Load(3'b000), .I_type_except_load(3'b000), .S_type(3'b001), .U_type(3'b011), .SB_type(3'b010),
    .jalr(3'b000), .UJ_type(3'b100), .in_9(instruction[6:2]), .To_Control(ImmSel));  // open: R_type
  OpSelect opselect_6 (
    .Load(1'b0), .I_type_except_load(1'b0), .S_type(1'b0), .R_type(1'b0), .U_type(1'b0),
    .SB_type(multiplexer_9_out), .jalr(1'b0), .UJ_type(1'b0), .in_9(instruction[6:2]), .To_Control(BrUn));

  assign LoadSel = instruction[13:12];

  // Other names for the same wires on the sheet: opcode[6:0] = instruction[6:0]; funct3[2:0] = instruction[14:12];
  //   funct7[6:0] = instruction[31:25]
endmodule

module OpSelect (
  input  Load,
  input  I_type_except_load,
  input  S_type,
  input  R_type,
  input  U_type,
  input  SB_type,
  input  jalr,
  input  UJ_type,
  input  [4:0] in_9,
  output To_Control
);

  Multiplexer #(.select(5), .enable("false")) multiplexer_1 (
    .in0(Load), .in4(I_type_except_load), .in8(S_type), .in12(R_type), .in13(U_type), .in24(SB_type),
    .in25(jalr), .in27(UJ_type), .out(To_Control), .sel(in_9));  // open: in1, in2, in3, in5, in6, in7, in9, in10, in11, in14, in15, in16, in17, in18, in19, in20, in21, in22, in23, in26, in28, in29, in30, in31
endmodule

module WBSelector (
  input  [1:0] Load,
  input  [1:0] I_type_except_load,
  input  [1:0] S_type,
  input  [1:0] R_type,
  input  [1:0] U_type,
  input  [1:0] SB_type,
  input  [1:0] jalr,
  input  [1:0] UJ_type,
  input  [4:0] in_9,
  output [1:0] To_Control
);

  Multiplexer #(.select(5), .width(2), .enable("false")) multiplexer_1 (
    .in0(Load), .in4(I_type_except_load), .in8(S_type), .in12(R_type), .in13(U_type), .in24(SB_type),
    .in25(jalr), .in27(UJ_type), .out(To_Control), .sel(in_9));  // open: in1, in2, in3, in5, in6, in7, in9, in10, in11, in14, in15, in16, in17, in18, in19, in20, in21, in22, in23, in26, in28, in29, in30, in31
endmodule

module ALUSelector (
  input  [3:0] Load,
  input  [3:0] I_type_except_load,
  input  [3:0] S_type,
  input  [3:0] R_type,
  input  [3:0] U_type,
  input  [3:0] SB_type,
  input  [3:0] jalr,
  input  [3:0] UJ_type,
  input  [4:0] in_9,
  output [3:0] To_Control
);

  Multiplexer #(.select(5), .width(4), .enable("false")) multiplexer_1 (
    .in0(Load), .in4(I_type_except_load), .in8(S_type), .in12(R_type), .in13(U_type), .in24(SB_type),
    .in25(jalr), .in27(UJ_type), .out(To_Control), .sel(in_9));  // open: in1, in2, in3, in5, in6, in7, in9, in10, in11, in14, in15, in16, in17, in18, in19, in20, in21, in22, in23, in26, in28, in29, in30, in31
endmodule

module ImmSelector (
  input  [2:0] Load,
  input  [2:0] I_type_except_load,
  input  [2:0] S_type,
  input  [2:0] R_type,
  input  [2:0] U_type,
  input  [2:0] SB_type,
  input  [2:0] jalr,
  input  [2:0] UJ_type,
  input  [4:0] in_9,
  output [2:0] To_Control
);

  Multiplexer #(.select(5), .width(3), .enable("false")) multiplexer_1 (
    .in0(Load), .in4(I_type_except_load), .in8(S_type), .in12(R_type), .in13(U_type), .in24(SB_type),
    .in25(jalr), .in27(UJ_type), .out(To_Control), .sel(in_9));  // open: in1, in2, in3, in5, in6, in7, in9, in10, in11, in14, in15, in16, in17, in18, in19, in20, in21, in22, in23, in26, in28, in29, in30, in31
endmodule
