// Logisim project regfile.circ as structural Verilog: 3 circuits, main circuit main
module main (
  input  [4:0] Read_Register_1__rs1,
  input  [4:0] Read_Register_2__rs2,
  input  [4:0] Write_Register__rd,
  input  [31:0] Write_Data,
  input  Write_Enable,
  input  Clock,
  output [31:0] s0_Value,
  output [31:0] s1_Value,
  output [31:0] t0_Value,
  output [31:0] t1_Value,
  output [31:0] a0_Value,
  output [31:0] ra_Value,
  output [31:0] sp_Value,
  output [31:0] Read_Data_1,
  output [31:0] Read_Data_2
);

  wire en0, en1, en2, en5, en6, en8, en9, en10, en11;
  wire [31:0] val0, val11;

  Register #(.width(32)) x0_zero (.D(Write_Data), .en(1'b0), .Q(val0), .clk(Clock));  // open: clr
  Register #(.width(32)) x1_ra (.D(Write_Data), .en(en1), .Q(ra_Value), .clk(Clock));  // open: clr
  en_demux en_demux_1 (
    .in_1(Write_Enable), .in_2(Write_Register__rd), .out_3(en0), .out_4(en1), .out_5(en2), .out_6(en5),
    .out_7(en6), .out_8(en8), .out_9(en9), .out_10(en10), .out_11(en11));
  Register #(.width(32)) x2_sp (.D(Write_Data), .en(en2), .Q(sp_Value), .clk(Clock));  // open: clr
  Register #(.width(32)) x5_t0 (.D(Write_Data), .en(en5), .Q(t0_Value), .clk(Clock));  // open: clr
  Register #(.width(32)) x6_t1 (.D(Write_Data), .en(en6), .Q(t1_Value), .clk(Clock));  // open: clr
  Register #(.width(32)) x8_s0 (.D(Write_Data), .en(en8), .Q(s0_Value), .clk(Clock));  // open: clr
  rs_mux rs_mux_1 (
    .in_1(val0), .in_2(ra_Value), .in_3(sp_Value), .in_4(t0_Value), .in_5(t1_Value), .in_6(s0_Value),
    .in_10(s1_Value), .in_8(a0_Value), .in_9(val11), .in_7(Read_Register_1__rs1), .out_11(Read_Data_1));
  Register #(.width(32)) x9_s1 (.D(Write_Data), .en(en9), .Q(s1_Value), .clk(Clock));  // open: clr
  Register #(.width(32)) x11_a1 (.D(Write_Data), .en(en11), .Q(val11), .clk(Clock));  // open: clr
  Register #(.width(32)) x10_a0 (.D(Write_Data), .en(en10), .Q(a0_Value), .clk(Clock));  // open: clr
  rs_mux rs_mux_2 (
    .in_1(val0), .in_2(ra_Value), .in_3(sp_Value), .in_4(t0_Value), .in_5(t1_Value), .in_6(s0_Value),
    .in_10(s1_Value), .in_8(a0_Value), .in_9(val11), .in_7(Read_Register_2__rs2), .out_11(Read_Data_2));

  // Other names for the same wires on the sheet: clk = Clock; read_data1[31:0] = Read_Data_1;
  //   read_data2[31:0] = Read_Data_2; read_reg1[4:0] = Read_Register_1__rs1; read_reg2[4:0] = Read_Register_2__rs2;
  //   val1[31:0] = ra_Value; val2[31:0] = sp_Value; val5[31:0] = t0_Value; val6[31:0] = t1_Value;
  //   val8[31:0] = s0_Value; val9[31:0] = s1_Value; val10[31:0] = a0_Value; write_en = Write_Enable;
  //   write_reg[4:0] = Write_Register__rd

  // Notes on the sheet:
  //   INPUTS to your circuit
  //   These are DEBUG/TEST outputs from your circuit.
  //   DON'T CHANGE THE LOCATIONS OF THE INPUTS AND OUTPUTS!
  //   OUTPUTS from your circuit
endmodule

module rs_mux (
  input  [31:0] in_1,
  input  [31:0] in_2,
  input  [31:0] in_3,
  input  [31:0] in_4,
  input  [31:0] in_5,
  input  [31:0] in_6,
  input  [4:0] in_7,
  input  [31:0] in_8,
  input  [31:0] in_9,
  input  [31:0] in_10,
  output [31:0] out_11
);

  Multiplexer #(.select(5), .width(32), .disabled(0), .enable("false")) multiplexer_1 (
    .in0(in_1), .in1(in_2), .in2(in_3), .in5(in_4), .in6(in_5), .in8(in_6), .in9(in_10), .in10(in_8),
    .in11(in_9), .out(out_11), .sel(in_7));  // open: in3, in4, in7, in12, in13, in14, in15, in16, in17, in18, in19, in20, in21, in22, in23, in24, in25, in26, in27, in28, in29, in30, in31
endmodule

module en_demux (
  input  in_1,
  input  [4:0] in_2,
  output out_3,
  output out_4,
  output out_5,
  output out_6,
  output out_7,
  output out_8,
  output out_9,
  output out_10,
  output out_11
);

  Demultiplexer #(.select(5), .disabled(0), .enable("false")) demultiplexer_1 (
    .out0(out_3), .out1(out_4), .out2(out_5), .out5(out_6), .out6(out_7), .out8(out_8), .out9(out_9),
    .out10(out_10), .out11(out_11), .in(in_1), .sel(in_2));  // open: out3, out4, out7, out12, out13, out14, out15, out16, out17, out18, out19, out20, out21, out22, out23, out24, out25, out26, out27, out28, out29, out30, out31
endmodule
