// Logisim project alu-mult.circ as structural Verilog: 1 circuit, main circuit main
module main (
  output halt,
  output [7:0] Test_num,
  output Equal,
  output [31:0] Result
);

  wire clock_1_out;
  wire [3:0] rom_3_data;
  wire [7:0] adder_1_out;
  wire [31:0] rom_1_data, rom_2_data;

  Clock clock_1 (.out(clock_1_out));
  Adder adder_1 (.a(8'h1), .b(Test_num), .out(adder_1_out));  // open: cin, cout
  Register register_1 (.D(adder_1_out), .Q(Test_num), .clk(clock_1_out));  // open: en, clr
  Comparator #(.mode("unsigned")) comparator_1 (.a(8'h3), .b(Test_num), .eq(halt));  // open: gt, lt
  ROM #(.dataWidth(32)) rom_1 (.addr(Test_num), .data(rom_1_data));  // open: sel
  ROM #(.dataWidth(32)) rom_2 (.addr(Test_num), .data(rom_2_data));  // open: sel
  ROM #(.dataWidth(4)) rom_3 (.addr(Test_num), .data(rom_3_data));  // open: sel
  alu_main main_1 (.Switch(rom_3_data), .X(rom_1_data), .Equal(Equal), .Result(Result), .Y(rom_2_data));
  // Probe on Result

  // Notes on the sheet:
  //   contents of rom_1 (hex, n*v repeats v):
  //   123 ffffdead ffffdead ffffffff
  //   contents of rom_2 (hex, n*v repeats v):
  //   15 ffffbeef ffffbeef 1
  //   contents of rom_3 (hex, n*v repeats v):
  //   7 7 8 8
  //   YOUR ALU SHOULD FIT HERE
  //   There should be no blue/red wires here, and the result shouldn't be x's.
endmodule
